# Fritzing sketch Robot_PowerRegulator_v0.1 (saved by Fritzing 0.8.0b)
stripboards: 1

parts:
  J2 = male pin header, 2 pins [form="♂ (male)"]
  J9_-_Outout = male pin header, 3 pins [form="♂ (male)"]
  Power = LED - 5mm [color="Red (633nm)" package="5 mm [THT]"]
  VCC1_6xAAA = Battery block 9V
  VCC2_-_9v_block = Battery block 9V
  J1 = male pin header, 2 pins [form="♂ (male)"]
  C4 = Electrolytic Capacitor [capacitance=100nF package="100 mil [THT, electrolytic]"]
  C3 = Electrolytic Capacitor [capacitance=4.7mF package="100 mil [THT, electrolytic]"]
  R1 = Resistor [tolerance=±5% resistance=220 package=THT]
  U1 = Voltage Regulator - 5V [package="TO220 [THT]"]
  1A = Fuse with Handler [part_number=Htc-15m]

nets:
  N1: J2.pin1, VCC2_-_9v_block.+
  N2: J2.pin2, J9_-_Outout.pin1
  GND: J9_-_Outout.pin2, VCC1_6xAAA.-, VCC2_-_9v_block.-, C4.-, C3.-, R1.Pin_1, U1.GND
  N3: J9_-_Outout.pin3, Power.anode, C4.+, C3.+, U1.output_voltage
  N4: Power.cathode, R1.Pin_0
  N5: VCC1_6xAAA.+, 1A.Connector2
  N6: J1.pin1, U1.input_voltage
  N7: J1.pin2, 1A.Connector1
